# Fritzing sketch Diagrama_BLE (saved by Fritzing 0.8.7b)
breadboards: 1

parts:
  Part2 = Arduino Uno (Rev3)
  M1 = DC Motor  # not connected
  M2 = DC Motor
  IC1 = L293D [package=THT]
  S1 = Toggle Switch [package=THT]  # not connected

nets:
  N1: Part2.D11_PWM/MOSI, IC1.Enable_1
  N2: Part2.D12/MISO, IC1.In_2
  N3: Part2.D13/SCK, IC1.In_1
  N4: Part2.5V, IC1.+V
  N5: Part2.GND, IC1.0V
  N6: M2.pin_1, IC1.Out_2_(_Controlled_by_Enable_1_)
  N7: M2.pin_2, IC1.Out_1_(_Controlled_by_Enable_1_)
